// Logisim project cpu.circ as structural Verilog
module Enabler8 (
  input  enable,
  input  in0,
  input  in1,
  input  in2,
  input  in3,
  input  in4,
  input  in5,
  input  in6,
  input  in7,
  output out0,
  output out1,
  output out2,
  output out3,
  output out4,
  output out6,
  output out6_2,
  output out7
);

  assign out0 = enable ? in0 : 1'bz;  // Controlled_Buffer controlled_buffer_1
  assign out1 = enable ? in1 : 1'bz;  // Controlled_Buffer controlled_buffer_2
  assign out2 = enable ? in2 : 1'bz;  // Controlled_Buffer controlled_buffer_3
  assign out3 = enable ? in3 : 1'bz;  // Controlled_Buffer controlled_buffer_4
  assign out4 = enable ? in4 : 1'bz;  // Controlled_Buffer controlled_buffer_5
  assign out6 = enable ? in5 : 1'bz;  // Controlled_Buffer controlled_buffer_6
  assign out6_2 = enable ? in6 : 1'bz;  // Controlled_Buffer controlled_buffer_7
  assign out7 = enable ? in7 : 1'bz;  // Controlled_Buffer controlled_buffer_8
endmodule

module Register8 (
  input  read,
  input  write,
  input  reset,
  input  in0,
  input  in1,
  input  in2,
  input  in3,
  input  in4,
  input  in5,
  input  in6,
  input  in7,
  output out0,
  output out1,
  output out2,
  output out3,
  output out4,
  output out5,
  output out6,
  output out7
);

  Reg4 reg4_1 (
    .in0(in0), .in1(in1), .in2(in2), .in3(in3), .read(read), .write(write), .out0(out0), .out1(out1),
    .out2(out2), .out3(out3), .reset(reset));
  Reg4 reg4_2 (
    .in0(in4), .in1(in5), .in2(in6), .in3(in7), .read(read), .write(write), .out0(out4), .out1(out5),
    .out2(out6), .out3(out7), .reset(reset));
endmodule

module DLatch (
  input  data,
  input  write,
  input  reset,
  output out
);

  wire nand_1_out, nand_2_out, nand_3_out, nand_4_out, nand_6_out;

  nand nand_1 (nand_1_out, data, data);
  nand nand_2 (nand_2_out, data, write);
  nand nand_3 (nand_3_out, write, nand_1_out);
  nand nand_4 (nand_4_out, reset, reset);
  nand nand_5 (out, nand_2_out, nand_6_out);
  nand nand_6 (nand_6_out, out, nand_3_out, nand_4_out);
endmodule

module Reg4 (
  input  in0,
  input  in1,
  input  in2,
  input  in3,
  input  read,
  input  write,
  input  reset,
  output out0,
  output out1,
  output out2,
  output out3
);

  wire dlatch_1_out, dlatch_2_out, dlatch_3_out, dlatch_4_out;

  assign out0 = read ? dlatch_1_out : 1'bz;  // Controlled_Buffer controlled_buffer_1
  DLatch dlatch_1 (.data(in0), .write(write), .out(dlatch_1_out), .reset(reset));
  DLatch dlatch_2 (.data(in1), .write(write), .out(dlatch_2_out), .reset(reset));
  assign out1 = read ? dlatch_2_out : 1'bz;  // Controlled_Buffer controlled_buffer_2
  DLatch dlatch_3 (.data(in2), .write(write), .out(dlatch_3_out), .reset(reset));
  assign out2 = read ? dlatch_3_out : 1'bz;  // Controlled_Buffer controlled_buffer_3
  DLatch dlatch_4 (.data(in3), .write(write), .out(dlatch_4_out), .reset(reset));
  assign out3 = read ? dlatch_4_out : 1'bz;  // Controlled_Buffer controlled_buffer_4
endmodule

module Ram256 (
  input  addr0,
  input  addr1,
  input  addr2,
  input  addr3,
  input  addr4,
  input  addr5,
  input  addr6,
  input  addr7,
  input  marw,
  input  read,
  input  write,
  input  clk,
  input  reset,
  input  in0,
  input  in1,
  input  in2,
  input  in3,
  input  in4,
  input  in5,
  input  in6,
  input  in7,
  output out0,
  output out1,
  output out2,
  output out3,
  output out4,
  output out5,
  output out6,
  output out7
);

  wire delayer_1_out, or_1_out;
  wire [7:0] MAR_out0;

  Register8 MAR (
    .in0(addr0), .in1(addr1), .in2(addr2), .in3(addr3), .in4(addr4), .in5(addr5), .in6(addr6), .in7(addr7),
    .read(1'b1), .write(marw), .reset(reset), .out0(MAR_out0[0]), .out1(MAR_out0[1]), .out2(MAR_out0[2]),
    .out3(MAR_out0[3]), .out4(MAR_out0[4]), .out5(MAR_out0[5]), .out6(MAR_out0[6]), .out7(MAR_out0[7]));
  Delayer delayer_1 (.in(clk), .out(delayer_1_out));
  or or_1 (or_1_out, read, write);
  RAM #(.bus("separate")) ram_1 (
    .addr(MAR_out0), .din({in7, in6, in5, in4, in3, in2, in1, in0}),
    .data({out7, out6, out5, out4, out3, out2, out1, out0}), .str(write), .sel(or_1_out),
    .clk(delayer_1_out), .ld(read), .clr(reset));
endmodule

module LeftShifter8 (
  input  cin,
  input  in0,
  input  in1,
  input  in2,
  input  in3,
  input  in4,
  input  in5,
  input  in6,
  input  in7,
  output out0,
  output out1,
  output out2,
  output out3,
  output out4,
  output out6,
  output out6_2,
  output out7,
  output cout
);


  assign cout = in7;
  assign out0 = cin;
  assign out1 = in0;
  assign out2 = in1;
  assign out3 = in2;
  assign out4 = in3;
  assign out6 = in4;
  assign out6_2 = in5;
  assign out7 = in6;
endmodule

module RightShifter8 (
  input  in0,
  input  in1,
  input  in2,
  input  in3,
  input  in4,
  input  in5,
  input  in6,
  input  in7,
  input  cin,
  output cout,
  output out0,
  output out1,
  output out2,
  output out3,
  output out4,
  output out6,
  output out6_2,
  output out7
);


  assign cout = in0;
  assign out0 = in1;
  assign out1 = in2;
  assign out2 = in3;
  assign out3 = in4;
  assign out4 = in5;
  assign out6 = in6;
  assign out6_2 = in7;
  assign out7 = cin;
endmodule

module Notter8 (
  input  in0,
  input  in1,
  input  in2,
  input  in3,
  input  in4,
  input  in5,
  input  in6,
  input  in7,
  output out0,
  output out1,
  output out2,
  output out3,
  output out4,
  output out6,
  output out6_2,
  output out7
);

  not not_1 (out0, in0);
  not not_2 (out1, in1);
  not not_3 (out2, in2);
  not not_4 (out3, in3);
  not not_5 (out4, in4);
  not not_6 (out6, in5);
  not not_7 (out6_2, in6);
  not not_8 (out7, in7);
endmodule

module Ander8 (
  input  a0,
  input  b0,
  input  a1,
  input  b1,
  input  a2,
  input  b2,
  input  a3,
  input  b3,
  input  a4,
  input  b4,
  input  a5,
  input  b5,
  input  a6,
  input  b6,
  input  a7,
  input  b7,
  output out0,
  output out1,
  output out2,
  output out3,
  output out4,
  output out5,
  output out6,
  output out7
);

  and and_1 (out0, a0, b0);
  and and_2 (out1, a1, b1);
  and and_3 (out2, a2, b2);
  and and_4 (out3, a3, b3);
  and and_5 (out4, a4, b4);
  and and_6 (out5, a5, b5);
  and and_7 (out6, a6, b6);
  and and_8 (out7, a7, b7);
endmodule

module Orer8 (
  input  a0,
  input  b0,
  input  a1,
  input  b1,
  input  a2,
  input  b2,
  input  a3,
  input  b3,
  input  a4,
  input  b4,
  input  a5,
  input  b5,
  input  a6,
  input  b6,
  input  a7,
  input  b7,
  output out0,
  output out1,
  output out2,
  output out3,
  output out4,
  output out5,
  output out6,
  output out7
);

  or or_1 (out0, a0, b0);
  or or_2 (out1, a1, b1);
  or or_3 (out2, a2, b2);
  or or_4 (out3, a3, b3);
  or or_5 (out4, a4, b4);
  or or_6 (out5, a5, b5);
  or or_7 (out6, a6, b6);
  or or_8 (out7, a7, b7);
endmodule

module Xorer8 (
  input  a0,
  input  b0,
  input  a1,
  input  b1,
  input  a2,
  input  b2,
  input  a3,
  input  b3,
  input  a4,
  input  b4,
  input  a5,
  input  b5,
  input  a6,
  input  b6,
  input  a7,
  input  b7,
  output out0,
  output out1,
  output out2,
  output out3,
  output out4,
  output out5,
  output out6,
  output out7
);

  xor xor_1 (out0, a0, b0);
  xor xor_2 (out1, a1, b1);
  xor xor_3 (out2, a2, b2);
  xor xor_4 (out3, a3, b3);
  xor xor_5 (out4, a4, b4);
  xor xor_6 (out5, a5, b5);
  xor xor_7 (out6, a6, b6);
  xor xor_8 (out7, a7, b7);
endmodule

module FullAdd (
  input  a,
  input  b,
  input  cin,
  output sum,
  output cout
);

  wire and_1_out, and_2_out, xor_1_out;

  xor xor_1 (xor_1_out, a, b);
  xor xor_2 (sum, xor_1_out, cin);
  and and_1 (and_1_out, xor_1_out, cin);
  and and_2 (and_2_out, a, b);
  or or_1 (cout, and_1_out, and_2_out);
endmodule

module Adder8 (
  input  cin,
  input  a0,
  input  b0,
  input  a1,
  input  b1,
  input  a2,
  input  b2,
  input  a3,
  input  b3,
  input  a4,
  input  b4,
  input  a5,
  input  b5,
  input  a6,
  input  b6,
  input  a7,
  input  b7,
  output out0,
  output out1,
  output out2,
  output out3,
  output out4,
  output out5,
  output out6,
  output out7,
  output ovcarry,
  output cout
);

  wire fulladd_1_cout, fulladd_2_cout, fulladd_3_cout, fulladd_4_cout, fulladd_5_cout, fulladd_6_cout;

  FullAdd fulladd_1 (.a(a0), .b(b0), .cin(cin), .sum(out0), .cout(fulladd_1_cout));
  FullAdd fulladd_2 (.a(a1), .b(b1), .cin(fulladd_1_cout), .sum(out1), .cout(fulladd_2_cout));
  FullAdd fulladd_3 (.a(a2), .b(b2), .cin(fulladd_2_cout), .sum(out2), .cout(fulladd_3_cout));
  FullAdd fulladd_4 (.a(a3), .b(b3), .cin(fulladd_3_cout), .sum(out3), .cout(fulladd_4_cout));
  FullAdd fulladd_5 (.a(a4), .b(b4), .cin(fulladd_4_cout), .sum(out4), .cout(fulladd_5_cout));
  FullAdd fulladd_6 (.a(a5), .b(b5), .cin(fulladd_5_cout), .sum(out5), .cout(fulladd_6_cout));
  FullAdd fulladd_7 (.a(a6), .b(b6), .cin(fulladd_6_cout), .sum(out6), .cout(ovcarry));
  FullAdd fulladd_8 (.a(a7), .b(b7), .cin(ovcarry), .sum(out7), .cout(cout));
endmodule

module AddSub8 (
  input  sub,
  input  a0,
  input  b0,
  input  a1,
  input  b1,
  input  a2,
  input  b2,
  input  a3,
  input  b3,
  input  a4,
  input  b4,
  input  a5,
  input  b5,
  input  a6,
  input  b6,
  input  a7,
  input  b7,
  input  cin,
  output carry,
  output overflow,
  output out7,
  output out6,
  output out5,
  output out4,
  output out3,
  output out2,
  output out1,
  output out0
);

  wire adder8_1_cout, adder8_1_ovcarry, xor_3_out, xor_4_out, xor_5_out, xor_6_out, xor_7_out, xor_8_out,
       xor_9_out, xor_10_out, xor_11_out;

  xor xor_1 (carry, sub, adder8_1_cout);
  xor xor_2 (overflow, adder8_1_ovcarry, adder8_1_cout);
  xor xor_3 (xor_3_out, sub, b0);
  xor xor_4 (xor_4_out, sub, b1);
  xor xor_5 (xor_5_out, sub, b2);
  xor xor_6 (xor_6_out, sub, b3);
  xor xor_7 (xor_7_out, sub, b4);
  xor xor_8 (xor_8_out, sub, b5);
  xor xor_9 (xor_9_out, sub, b6);
  xor xor_10 (xor_10_out, sub, b7);
  Adder8 adder8_1 (
    .cin(xor_11_out), .a0(a0), .b0(xor_3_out), .a1(a1), .b1(xor_4_out), .a2(a2), .b2(xor_5_out), .a3(a3),
    .b3(xor_6_out), .a4(a4), .b4(xor_7_out), .a5(a5), .b5(xor_8_out), .a6(a6), .b6(xor_9_out), .a7(a7),
    .b7(xor_10_out), .out0(out0), .out1(out1), .out2(out2), .out3(out3), .out4(out4), .out5(out5),
    .out6(out6), .out7(out7), .ovcarry(adder8_1_ovcarry), .cout(adder8_1_cout));
  xor xor_11 (xor_11_out, sub, cin);
endmodule

module Bus0Gate (
  input  in7,
  input  in6,
  input  in5,
  input  in4,
  input  in3,
  input  in2,
  input  in1,
  input  in0,
  input  bus_0,
  output out7,
  output out6,
  output out5,
  output out4,
  output out3,
  output out2,
  output out1,
  output out0
);

  wire not_1_out;

  and and_1 (out7, in7, not_1_out);
  and and_2 (out6, in6, not_1_out);
  and and_3 (out5, in5, not_1_out);
  and and_4 (out4, in4, not_1_out);
  and and_5 (out3, in3, not_1_out);
  and and_6 (out2, in2, not_1_out);
  and and_7 (out1, in1, not_1_out);
  not not_1 (not_1_out, bus_0);
  and and_8 (out0, in0, not_1_out);
endmodule

module ALUnit (
  input  a7,
  input  a6,
  input  a5,
  input  a4,
  input  a3,
  input  a2,
  input  a1,
  input  a0,
  input  b7,
  input  b6,
  input  b5,
  input  b4,
  input  b3,
  input  b2,
  input  b1,
  input  b0,
  input  op2,
  input  op1,
  input  op0,
  input  cin,
  output out0,
  output out1,
  output out2,
  output out3,
  output out4,
  output out5,
  output out6,
  output out7,
  output overflow,
  output carry,
  output sign,
  output zero
);

  wire addsub8_1_carry, addsub8_1_out0, addsub8_1_out1, addsub8_1_out2, addsub8_1_out3, addsub8_1_out4,
       addsub8_1_out5, addsub8_1_out6, addsub8_1_out7, addsub8_1_overflow, ander8_1_out0, ander8_1_out1,
       ander8_1_out2, ander8_1_out3, ander8_1_out4, ander8_1_out5, ander8_1_out6, ander8_1_out7,
       leftshifter8_1_cout, leftshifter8_1_out0, leftshifter8_1_out1, leftshifter8_1_out2,
       leftshifter8_1_out3, leftshifter8_1_out4, leftshifter8_1_out6, leftshifter8_1_out6_2,
       leftshifter8_1_out7, nor_2_out, or_1_out, orer8_1_out0, orer8_1_out1, orer8_1_out2, orer8_1_out3,
       orer8_1_out4, orer8_1_out5, orer8_1_out6, orer8_1_out7, rightshifter8_1_cout, rightshifter8_1_out0,
       rightshifter8_1_out1, rightshifter8_1_out2, rightshifter8_1_out3, rightshifter8_1_out4,
       rightshifter8_1_out6, rightshifter8_1_out6_2, rightshifter8_1_out7, xorer8_1_out0, xorer8_1_out1,
       xorer8_1_out2, xorer8_1_out3, xorer8_1_out4, xorer8_1_out5, xorer8_1_out6, xorer8_1_out7;
  wire [7:0] decoder_1_out0;

  Ander8 ander8_1 (
    .a0(a0), .b0(b0), .a1(a1), .b1(b1), .a2(a2), .b2(b2), .a3(a3), .b3(b3), .a4(a4), .b4(b4), .a5(a5),
    .b5(b5), .a6(a6), .b6(b6), .a7(a7), .b7(b7), .out0(ander8_1_out0), .out1(ander8_1_out1),
    .out2(ander8_1_out2), .out3(ander8_1_out3), .out4(ander8_1_out4), .out5(ander8_1_out5),
    .out6(ander8_1_out6), .out7(ander8_1_out7));
  Orer8 orer8_1 (
    .a0(a0), .b0(b0), .a1(a1), .b1(b1), .a2(a2), .b2(b2), .a3(a3), .b3(b3), .a4(a4), .b4(b4), .a5(a5),
    .b5(b5), .a6(a6), .b6(b6), .a7(a7), .b7(b7), .out0(orer8_1_out0), .out1(orer8_1_out1),
    .out2(orer8_1_out2), .out3(orer8_1_out3), .out4(orer8_1_out4), .out5(orer8_1_out5), .out6(orer8_1_out6),
    .out7(orer8_1_out7));
  Xorer8 xorer8_1 (
    .a0(a0), .b0(b0), .a1(a1), .b1(b1), .a2(a2), .b2(b2), .a3(a3), .b3(b3), .a4(a4), .b4(b4), .a5(a5),
    .b5(b5), .a6(a6), .b6(b6), .a7(a7), .b7(b7), .out0(xorer8_1_out0), .out1(xorer8_1_out1),
    .out2(xorer8_1_out2), .out3(xorer8_1_out3), .out4(xorer8_1_out4), .out5(xorer8_1_out5),
    .out6(xorer8_1_out6), .out7(xorer8_1_out7));
  AddSub8 addsub8_1 (
    .cin(cin), .a0(a0), .b0(b0), .a1(a1), .b1(b1), .a2(a2), .b2(b2), .a3(a3), .b3(b3), .a4(a4), .b4(b4),
    .a5(a5), .b5(b5), .a6(a6), .b6(b6), .a7(a7), .b7(b7), .out0(addsub8_1_out0), .out1(addsub8_1_out1),
    .out2(addsub8_1_out2), .out3(addsub8_1_out3), .out4(addsub8_1_out4), .out5(addsub8_1_out5),
    .out6(addsub8_1_out6), .out7(addsub8_1_out7), .carry(addsub8_1_carry), .sub(decoder_1_out0[5]),
    .overflow(addsub8_1_overflow));
  LeftShifter8 leftshifter8_1 (
    .cin(cin), .in0(a0), .in1(a1), .in2(a2), .in3(a3), .in4(a4), .in5(a5), .in6(a6), .in7(a7),
    .out0(leftshifter8_1_out0), .out1(leftshifter8_1_out1), .out2(leftshifter8_1_out2),
    .out3(leftshifter8_1_out3), .out4(leftshifter8_1_out4), .out6(leftshifter8_1_out6),
    .out6_2(leftshifter8_1_out6_2), .out7(leftshifter8_1_out7), .cout(leftshifter8_1_cout));
  RightShifter8 rightshifter8_1 (
    .in0(a0), .in1(a1), .in2(a2), .in3(a3), .in4(a4), .in5(a5), .in6(a6), .in7(a7), .cin(cin),
    .cout(rightshifter8_1_cout), .out0(rightshifter8_1_out0), .out1(rightshifter8_1_out1),
    .out2(rightshifter8_1_out2), .out3(rightshifter8_1_out3), .out4(rightshifter8_1_out4),
    .out6(rightshifter8_1_out6), .out6_2(rightshifter8_1_out6_2), .out7(rightshifter8_1_out7));
  Decoder #(.select(3), .enable("false")) decoder_1 (
    .out0(decoder_1_out0[0]), .out1(decoder_1_out0[1]), .out2(decoder_1_out0[2]), .out3(decoder_1_out0[3]),
    .out4(decoder_1_out0[4]), .out5(decoder_1_out0[5]), .out6(decoder_1_out0[6]), .out7(decoder_1_out0[7]),
    .sel({op2, op1, op0}));
  Enabler8 enabler8_1 (
    .in0(a0), .in1(a1), .in2(a2), .in3(a3), .in4(a4), .in5(a5), .in6(a6), .in7(a7),
    .enable(decoder_1_out0[0]), .out0(out0), .out1(out1), .out2(out2), .out3(out3), .out4(out4), .out6(out5),
    .out6_2(out6), .out7(out7));
  Enabler8 enabler8_2 (
    .in0(ander8_1_out0), .in1(ander8_1_out1), .in2(ander8_1_out2), .in3(ander8_1_out3), .in4(ander8_1_out4),
    .in5(ander8_1_out5), .in6(ander8_1_out6), .in7(ander8_1_out7), .enable(decoder_1_out0[1]), .out0(out0),
    .out1(out1), .out2(out2), .out3(out3), .out4(out4), .out6(out5), .out6_2(out6), .out7(out7));
  Enabler8 enabler8_3 (
    .in0(orer8_1_out0), .in1(orer8_1_out1), .in2(orer8_1_out2), .in3(orer8_1_out3), .in4(orer8_1_out4),
    .in5(orer8_1_out5), .in6(orer8_1_out6), .in7(orer8_1_out7), .enable(decoder_1_out0[2]), .out0(out0),
    .out1(out1), .out2(out2), .out3(out3), .out4(out4), .out6(out5), .out6_2(out6), .out7(out7));
  Enabler8 enabler8_4 (
    .in0(xorer8_1_out0), .in1(xorer8_1_out1), .in2(xorer8_1_out2), .in3(xorer8_1_out3), .in4(xorer8_1_out4),
    .in5(xorer8_1_out5), .in6(xorer8_1_out6), .in7(xorer8_1_out7), .enable(decoder_1_out0[3]), .out0(out0),
    .out1(out1), .out2(out2), .out3(out3), .out4(out4), .out6(out5), .out6_2(out6), .out7(out7));
  or or_1 (or_1_out, decoder_1_out0[4], decoder_1_out0[5]);
  Enabler8 enabler8_5 (
    .in0(addsub8_1_out0), .in1(addsub8_1_out1), .in2(addsub8_1_out2), .in3(addsub8_1_out3),
    .in4(addsub8_1_out4), .in5(addsub8_1_out5), .in6(addsub8_1_out6), .in7(addsub8_1_out7),
    .enable(or_1_out), .out0(out0), .out1(out1), .out2(out2), .out3(out3), .out4(out4), .out6(out5),
    .out6_2(out6), .out7(out7));
  Enabler8 enabler8_6 (
    .in0(leftshifter8_1_out0), .in1(leftshifter8_1_out1), .in2(leftshifter8_1_out2),
    .in3(leftshifter8_1_out3), .in4(leftshifter8_1_out4), .in5(leftshifter8_1_out6),
    .in6(leftshifter8_1_out6_2), .in7(leftshifter8_1_out7), .enable(decoder_1_out0[6]), .out0(out0),
    .out1(out1), .out2(out2), .out3(out3), .out4(out4), .out6(out5), .out6_2(out6), .out7(out7));
  Enabler8 enabler8_7 (
    .in0(rightshifter8_1_out0), .in1(rightshifter8_1_out1), .in2(rightshifter8_1_out2),
    .in3(rightshifter8_1_out3), .in4(rightshifter8_1_out4), .in5(rightshifter8_1_out6),
    .in6(rightshifter8_1_out6_2), .in7(rightshifter8_1_out7), .enable(decoder_1_out0[7]), .out0(out0),
    .out1(out1), .out2(out2), .out3(out3), .out4(out4), .out6(out5), .out6_2(out6), .out7(out7));
  nor nor_1 (zero, out7, out6, out5, out4, out3, out2, out1, out0);
  Multiplexer #(.enable("false")) multiplexer_1 (.in0(1'b0), .in1(addsub8_1_overflow), .out(overflow), .sel(or_1_out));
  nor nor_2 (nor_2_out, or_1_out, decoder_1_out0[6], decoder_1_out0[7]);
  assign carry = nor_2_out ? 1'b0 : 1'bz;  // Controlled_Buffer controlled_buffer_1
  assign carry = or_1_out ? addsub8_1_carry : 1'bz;  // Controlled_Buffer controlled_buffer_2
  assign carry = decoder_1_out0[6] ? leftshifter8_1_cout : 1'bz;  // Controlled_Buffer controlled_buffer_3
  assign carry = decoder_1_out0[7] ? rightshifter8_1_cout : 1'bz;  // Controlled_Buffer controlled_buffer_4

  assign sign = out7;
endmodule

module Clock (
  input  clk,
  input  rst,
  output clk_r,
  output clk_w
);

  wire j_k_ff_1_q, j_k_ff_1_qn, nand_1_out, nand_2_out, not_1_out;

  not not_1 (not_1_out, clk);
  nand nand_1 (nand_1_out, clk, j_k_ff_1_q);
  J_K_Flip_Flop j_k_ff_1 (
    .J(1'b1), .clk(not_1_out), .K(1'b1), .Q(j_k_ff_1_q), .Qn(j_k_ff_1_qn), .preset(rst), .en(1'b1),
    .reset(1'b0));
  nand nand_2 (nand_2_out, j_k_ff_1_qn, clk);
  buf buffer_1 (clk_r, nand_1_out);
  not not_2 (clk_w, nand_2_out);
endmodule

module BranchChecker (
  input  zero,
  input  sign,
  input  carry,
  input  overflow,
  input  op2,
  input  op1,
  input  op0,
  output result
);

  wire and_1_out, and_2_out, and_3_out, and_4_out, and_5_out, and_6_out, and_7_out, decoder_1_out0,
       decoder_1_out1, decoder_1_out2, decoder_1_out3, decoder_1_out4, decoder_1_out5, decoder_1_out6,
       decoder_1_out7, or_1_out, or_2_out, xor_1_out;

  Decoder #(.select(3), .enable("false")) decoder_1 (
    .out0(decoder_1_out0), .out1(decoder_1_out1), .out2(decoder_1_out2), .out3(decoder_1_out3),
    .out4(decoder_1_out4), .out5(decoder_1_out5), .out6(decoder_1_out6), .out7(decoder_1_out7),
    .sel({op2, op1, op0}));
  or or_1 (or_1_out, zero, xor_1_out);
  or or_2 (or_2_out, carry, zero);
  xor xor_1 (xor_1_out, overflow, sign);
  and and_1 (and_1_out, decoder_1_out1, zero);
  and and_2 (and_2_out, decoder_1_out2, sign);
  and and_3 (and_3_out, decoder_1_out3, overflow);
  and and_4 (and_4_out, decoder_1_out4, carry);
  and and_5 (and_5_out, decoder_1_out5, or_2_out);
  and and_6 (and_6_out, decoder_1_out6, xor_1_out);
  and and_7 (and_7_out, decoder_1_out7, or_1_out);
  or or_3 (result, and_7_out, and_6_out, and_5_out, and_4_out, and_3_out, and_2_out, and_1_out, decoder_1_out0);
endmodule

module Control (
  input  rst,
  input  zero,
  input  sign,
  input  carry,
  input  overflow,
  input  clk,
  input  ir7,
  input  ir6,
  input  ir5,
  input  ir4,
  input  ir3,
  input  ir2,
  input  ir1,
  input  ir0,
  output rd_r,
  output ra_w,
  output rb_w,
  output bus_0,
  output io,
  output io_in_out,
  output io_data_addr,
  output rx_r,
  output rx_w,
  output fr_w,
  output rx1,
  output pc_w,
  output rx0,
  output pc_r,
  output ir_w,
  output cin,
  output mar_w,
  output op2,
  output ram_w,
  output op1,
  output op0,
  output ram_r,
  output halt,
  output new_cycle,
  output new_instr
);

  wire and_10_out, and_13_out, and_14_out, and_15_out, branchchecker_1_result, clock_1_clk_r, clock_1_clk_w,
       delayer_1_out, instr_state_qn, or_1_out, or_2_out, or_3_out;
  wire [1:0] multiplexer_2_out, multiplexer_3_out;
  wire [6:0] adder_1_out, mPC_q, multiplexer_1_out, rom_1_data;
  wire [6:6] instr_state_q;
  wire [31:4] rom_1_data_2;

  and and_1 (fr_w, rom_1_data_2[12], clock_1_clk_w);
  and and_2 (pc_w, rom_1_data_2[13], clock_1_clk_w);
  and and_3 (pc_r, rom_1_data_2[14], clock_1_clk_r);
  and and_4 (ir_w, rom_1_data_2[15], clock_1_clk_w);
  and and_5 (mar_w, rom_1_data_2[16], clock_1_clk_w);
  and and_6 (ram_w, rom_1_data_2[17], clock_1_clk_w);
  and and_7 (ram_r, rom_1_data_2[18], clock_1_clk_r);
  Clock clock_1 (.clk_r(clock_1_clk_r), .clk(clk), .clk_w(clock_1_clk_w), .rst(or_1_out));
  nor nor_1 (new_cycle, clock_1_clk_r, clock_1_clk_w);
  or or_1 (or_1_out, rst, halt);
  and and_8 (ra_w, clock_1_clk_w, rom_1_data_2[10]);
  and and_9 (rd_r, clock_1_clk_r, rom_1_data_2[11]);
  Register #(.width(7)) mPC (.D(multiplexer_1_out), .en(1'b1), .Q(mPC_q), .clk(new_cycle), .clr(or_1_out));
  Multiplexer #(.select(2), .width(7), .enable("false")) multiplexer_1 (
    .in0(adder_1_out), .in1(adder_1_out), .in2(rom_1_data),
    .in3({instr_state_q[6], ir7, ir6, ir5, ir4, 2'b00}), .out(multiplexer_1_out), .sel(multiplexer_2_out));
  and and_10 (and_10_out, clock_1_clk_w, rom_1_data_2[31]);
  and and_11 (rb_w, clock_1_clk_w, rom_1_data_2[9]);
  Delayer delayer_1 (.in(new_cycle), .out(delayer_1_out));
  and and_12 (new_instr, delayer_1_out, and_13_out);
  and and_13 (and_13_out, ~mPC_q[6], ~mPC_q[5], ~mPC_q[4], ~mPC_q[3], ~mPC_q[2], ~mPC_q[1], mPC_q[0]);  // AND_Gate
  Adder #(.width(7)) adder_1 (.a(mPC_q), .b({7{1'b0}}), .out(adder_1_out), .cin(1'b1));  // open: cout
  D_Flip_Flop instr_state (
    .clk(and_10_out), .D(instr_state_qn), .Q(instr_state_q[6]), .Qn(instr_state_qn), .en(1'b1),
    .reset(or_1_out));  // open: preset
  ROM #(.addrWidth(7), .dataWidth(32)) rom_1 (
    .addr(mPC_q),
    .data({rom_1_data_2[31:27], rom_1_data, halt, rom_1_data_2[18:9], bus_0, io, rom_1_data_2[6:4], cin, op2, op1, op0}),
    .sel(1'b1));
  Multiplexer #(.select(2), .width(2), .enable("false")) multiplexer_2 (
    .in0(2'b00), .in1(multiplexer_3_out), .in2(2'b10), .in3(2'b11), .out(multiplexer_2_out),
    .sel(rom_1_data_2[29:28]));
  and and_14 (and_14_out, ir3, io);
  and and_15 (and_15_out, io, ~ir3);  // AND_Gate
  BranchChecker branchchecker_1 (
    .zero(zero), .sign(sign), .carry(carry), .overflow(overflow), .op0(ir0), .op1(ir1), .op2(ir2),
    .result(branchchecker_1_result));
  Multiplexer #(.width(2), .enable("false")) multiplexer_3 (
    .in0(2'b00), .in1(2'b10), .out(multiplexer_3_out), .sel(branchchecker_1_result));
  or or_2 (or_2_out, rom_1_data_2[6], and_15_out);
  or or_3 (or_3_out, rom_1_data_2[5], and_14_out);
  Multiplexer #(.width(2), .enable("false")) multiplexer_4 (
    .in0({ir3, ir2}), .in1({ir1, ir0}), .out({rx1, rx0}), .sel(rom_1_data_2[4]));
  and and_16 (rx_r, clock_1_clk_r, or_2_out);
  and and_17 (rx_w, clock_1_clk_w, or_3_out);

  assign io_data_addr = ir2;
  assign io_in_out = ir3;

  // Notes on the sheet:
  //   Map instructions to 1xxxx00 with xxxx=OPCODE
  //   to avoid collision with IFETCH.
  //   Instructions must complete in 4 steps.
  //   0x00 has no instruction since after reset it won't be executed.
  //   00xy -> jump to addr mPC+1
  //   01xy -> branch to either addr mPC+1 or ROM[mPC]
  //   10xy -> jump to addr ROM[mPC]
  //   11xy -> jump to instr in IR
  //   contents of rom_1 (hex, n*v repeats v):
  //   0 14700 280c b0048000 60*0 450 a0100820 0 0 14700 280c a0140030 0 10050 a0140020 0 0 10050 a0120040
  //   0 0 4400 2050 a0100830 0 15614400 a0102b0c 40200 a0102804 a0080000 0 0 0 a0100000 0 0 0 440 250
  //   a0101824 0 440 250 a0101825 0 450 a0101826 0 0 450 a0101827 0 0 440 250 a0101821 0 440 250 a0101822
  //   0 440 250 a0101823 0 440 a0101255
endmodule

module Main (
  input  in_1,
  input  in_2,
  input  in_3,
  input  in_4,
  input  in_5,
  input  in_6,
  input  in_7,
  input  in_8,
  input  MANUAL,
  input  in_10,
  input  in_11,
  input  in_12,
  input  in_13,
  input  in_14,
  input  in_15,
  input  in_16,
  input  in_17,
  output out_18,
  output out_19,
  output out_20,
  output out_21,
  output out_22,
  output out_23,
  output out_24,
  output out_25
);

  wire ADDR_out, alunit_1_carry, alunit_1_out0, alunit_1_out1, alunit_1_out2, alunit_1_out3, alunit_1_out4,
       alunit_1_out5, alunit_1_out6, alunit_1_out7, alunit_1_overflow, alunit_1_sign, alunit_1_zero,
       and_1_out, and_2_out, and_3_out, and_4_out, and_5_out, and_6_out, and_7_out, and_8_out, and_9_out,
       and_10_out, and_11_out, and_12_out, bus0gate_1_out0, bus0gate_1_out1, bus0gate_1_out2,
       bus0gate_1_out3, bus0gate_1_out4, bus0gate_1_out5, bus0gate_1_out6, bus0gate_1_out7, CLOCK_out,
       control_1_bus_0, control_1_cin, control_1_fr_w, control_1_halt, control_1_ir_w, control_1_mar_w,
       control_1_new_cycle, control_1_new_instr, control_1_op0, control_1_op1, control_1_op2, control_1_pc_r,
       control_1_pc_w, control_1_ra_w, control_1_ram_r, control_1_ram_w, control_1_rb_w, control_1_rd_r,
       control_1_rx_r, control_1_rx_w, controlled_buffer_1_out, controlled_buffer_2_out, decoder_1_out0,
       decoder_1_out1, decoder_1_out2, decoder_1_out3, FR_out0, FR_out1, FR_out2, FR_out3, HALT_2_q,
       HALT_2_qn, LDR_out, not_1_out, not_2_out, not_3_out, or_1_out, or_2_out, or_3_out, or_4_out, or_5_out,
       or_6_out, or_7_out, RA_out0, RA_out1, RA_out2, RA_out3, RA_out4, RA_out5, RA_out6, RA_out7, RB_out0,
       RB_out1, RB_out2, RB_out3, RB_out4, RB_out5, RB_out6, RB_out7, RESET_2_out, RESET_3_out, RESUME_out,
       STEP_out, STR_out;
  wire [1:0] control_1_rx0;
  wire [3:0] CYCLES_q, CYCLES_q_2;
  wire [7:0] INSTR_q, IR_out0;

  ALUnit alunit_1 (
    .a7(RA_out7), .a6(RA_out6), .a5(RA_out5), .a4(RA_out4), .a3(RA_out3), .a2(RA_out2), .a1(RA_out1),
    .a0(RA_out0), .b7(RB_out7), .b6(RB_out6), .b5(RB_out5), .b4(RB_out4), .b3(RB_out3), .b2(RB_out2),
    .b1(RB_out1), .b0(RB_out0), .cin(control_1_cin), .op2(control_1_op2), .op1(control_1_op1),
    .op0(control_1_op0), .out0(alunit_1_out0), .out1(alunit_1_out1), .out2(alunit_1_out2),
    .out3(alunit_1_out3), .out4(alunit_1_out4), .out5(alunit_1_out5), .out6(alunit_1_out6),
    .out7(alunit_1_out7), .overflow(alunit_1_overflow), .sign(alunit_1_sign), .zero(alunit_1_zero),
    .carry(alunit_1_carry));
  LED Reset (.in(RESET_2_out));
  Button RESET_2 (.out(RESET_2_out));
  Button RESUME (.out(RESUME_out));
  not not_1 (not_1_out, MANUAL);
  assign controlled_buffer_1_out = MANUAL ? STEP_out : 1'bz;  // Controlled_Buffer controlled_buffer_1
  Button STEP (.out(STEP_out));
  Clock_part CLOCK (.out(CLOCK_out));
  Pull_Resistor pull_resistor_1 (.node(controlled_buffer_1_out));
  Register8 RA (
    .in0(out_25), .in1(out_24), .in2(out_23), .in3(out_22), .in4(out_21), .in5(out_20), .in6(out_19),
    .in7(out_18), .read(1'b1), .write(control_1_ra_w), .reset(RESET_2_out), .out0(RA_out0), .out1(RA_out1),
    .out2(RA_out2), .out3(RA_out3), .out4(RA_out4), .out5(RA_out5), .out6(RA_out6), .out7(RA_out7));
  LED Auto (.in(not_2_out));
  LED u_Manual (.in(MANUAL));
  not not_2 (not_2_out, MANUAL);
  or or_1 (or_1_out, controlled_buffer_1_out, controlled_buffer_2_out);
  assign controlled_buffer_2_out = not_1_out ? CLOCK_out : 1'bz;  // Controlled_Buffer controlled_buffer_2
  Pull_Resistor pull_resistor_2 (.node(controlled_buffer_2_out));
  Register8 RB (
    .in0(bus0gate_1_out0), .in1(bus0gate_1_out1), .in2(bus0gate_1_out2), .in3(bus0gate_1_out3),
    .in4(bus0gate_1_out4), .in5(bus0gate_1_out5), .in6(bus0gate_1_out6), .in7(bus0gate_1_out7), .read(1'b1),
    .write(control_1_rb_w), .reset(RESET_2_out), .out0(RB_out0), .out1(RB_out1), .out2(RB_out2),
    .out3(RB_out3), .out4(RB_out4), .out5(RB_out5), .out6(RB_out6), .out7(RB_out7));
  Register8 RD (
    .in0(alunit_1_out0), .in1(alunit_1_out1), .in2(alunit_1_out2), .in3(alunit_1_out3), .in4(alunit_1_out4),
    .in5(alunit_1_out5), .in6(alunit_1_out6), .in7(alunit_1_out7), .read(control_1_rd_r), .write(1'b1),
    .reset(RESET_2_out), .out0(out_25), .out1(out_24), .out2(out_23), .out3(out_22), .out4(out_21),
    .out5(out_20), .out6(out_19), .out7(out_18));
  LED Clock_2 (.in(or_1_out));
  LED Halt (.in(HALT_2_q));
  not not_3 (not_3_out, not_2_out);
  Bus0Gate bus0gate_1 (
    .bus_0(control_1_bus_0), .in7(out_18), .in6(out_19), .in5(out_20), .in4(out_21), .in3(out_22),
    .in2(out_23), .in1(out_24), .in0(out_25), .out7(bus0gate_1_out7), .out6(bus0gate_1_out6),
    .out5(bus0gate_1_out5), .out4(bus0gate_1_out4), .out3(bus0gate_1_out3), .out2(bus0gate_1_out2),
    .out1(bus0gate_1_out1), .out0(bus0gate_1_out0));
  and and_1 (and_1_out, ~HALT_2_q, or_1_out);  // AND_Gate
  Reg4 FR (
    .in0(alunit_1_zero), .in1(alunit_1_sign), .in2(alunit_1_carry), .in3(alunit_1_overflow), .read(1'b1),
    .write(control_1_fr_w), .out0(FR_out0), .out1(FR_out1), .out2(FR_out2), .out3(FR_out3),
    .reset(RESET_2_out));
  Control control_1 (
    .op0(control_1_op0), .op1(control_1_op1), .op2(control_1_op2), .fr_w(control_1_fr_w),
    .mar_w(control_1_mar_w), .ram_r(control_1_ram_r), .ram_w(control_1_ram_w), .carry(FR_out2),
    .sign(FR_out1), .zero(FR_out0), .ra_w(control_1_ra_w), .rb_w(control_1_rb_w), .bus_0(control_1_bus_0),
    .rx_r(control_1_rx_r), .rx_w(control_1_rx_w), .clk(and_1_out), .rst(RESET_2_out), .rd_r(control_1_rd_r),
    .ir0(IR_out0[0]), .ir1(IR_out0[1]), .ir2(IR_out0[2]), .ir3(IR_out0[3]), .ir4(IR_out0[4]),
    .ir5(IR_out0[5]), .ir6(IR_out0[6]), .ir7(IR_out0[7]), .ir_w(control_1_ir_w), .pc_w(control_1_pc_w),
    .pc_r(control_1_pc_r), .overflow(FR_out3), .halt(control_1_halt), .cin(control_1_cin),
    .new_instr(control_1_new_instr), .new_cycle(control_1_new_cycle), .rx0(control_1_rx0[0]),
    .rx1(control_1_rx0[1]));  // open: io_in_out, io_data_addr, io
  D_Flip_Flop HALT_2 (
    .clk(control_1_halt), .D(HALT_2_qn), .Q(HALT_2_q), .Qn(HALT_2_qn), .en(1'b1), .reset(or_2_out));  // open: preset
  or or_2 (or_2_out, RESUME_out, RESET_2_out);
  Register8 R0 (
    .in0(out_25), .in1(out_24), .in2(out_23), .in3(out_22), .in4(out_21), .in5(out_20), .in6(out_19),
    .in7(out_18), .read(and_2_out), .write(and_3_out), .reset(RESET_2_out), .out0(out_25), .out1(out_24),
    .out2(out_23), .out3(out_22), .out4(out_21), .out5(out_20), .out6(out_19), .out7(out_18));
  and and_2 (and_2_out, control_1_rx_r, decoder_1_out0);
  Decoder #(.select(2), .enable("false")) decoder_1 (
    .out0(decoder_1_out0), .out1(decoder_1_out1), .out2(decoder_1_out2), .out3(decoder_1_out3),
    .sel(control_1_rx0));
  Counter #(.trigger("falling")) INSTR (
    .load(1'b0), .count(1'b1), .Q(INSTR_q), .clk(control_1_new_instr), .clr(RESET_2_out));  // open: D, carry
  Hex_Digit_Display hex_digit_display_1 (.value(INSTR_q[3:0]));  // open: dp
  Hex_Digit_Display hex_digit_display_2 (.value(INSTR_q[7:4]));  // open: dp
  and and_3 (and_3_out, decoder_1_out0, control_1_rx_w);
  Counter CYCLES (
    .load(1'b0), .count(1'b1), .Q({CYCLES_q_2, CYCLES_q}), .clk(control_1_new_cycle), .clr(or_3_out));  // open: D, carry
  or or_3 (or_3_out, control_1_new_instr, RESET_2_out);
  Hex_Digit_Display hex_digit_display_3 (.value(CYCLES_q_2));  // open: dp
  Register8 IR (
    .in0(out_25), .in1(out_24), .in2(out_23), .in3(out_22), .in4(out_21), .in5(out_20), .in6(out_19),
    .in7(out_18), .read(1'b1), .write(control_1_ir_w), .reset(RESET_2_out), .out0(IR_out0[0]),
    .out1(IR_out0[1]), .out2(IR_out0[2]), .out3(IR_out0[3]), .out4(IR_out0[4]), .out5(IR_out0[5]),
    .out6(IR_out0[6]), .out7(IR_out0[7]));
  Hex_Digit_Display hex_digit_display_4 (.value(CYCLES_q));  // open: dp
  Register8 R1 (
    .in0(out_25), .in1(out_24), .in2(out_23), .in3(out_22), .in4(out_21), .in5(out_20), .in6(out_19),
    .in7(out_18), .read(and_5_out), .write(and_4_out), .reset(RESET_2_out), .out0(out_25), .out1(out_24),
    .out2(out_23), .out3(out_22), .out4(out_21), .out5(out_20), .out6(out_19), .out7(out_18));
  and and_4 (and_4_out, decoder_1_out1, control_1_rx_w);
  and and_5 (and_5_out, control_1_rx_r, decoder_1_out1);
  and and_6 (and_6_out, not_3_out, LDR_out);
  and and_7 (and_7_out, ADDR_out, not_3_out);
  Button ADDR (.out(ADDR_out));
  Button LDR (.out(LDR_out));
  Register8 R2 (
    .in0(out_25), .in1(out_24), .in2(out_23), .in3(out_22), .in4(out_21), .in5(out_20), .in6(out_19),
    .in7(out_18), .read(and_8_out), .write(and_10_out), .reset(RESET_2_out), .out0(out_25), .out1(out_24),
    .out2(out_23), .out3(out_22), .out4(out_21), .out5(out_20), .out6(out_19), .out7(out_18));
  and and_8 (and_8_out, control_1_rx_r, decoder_1_out2);
  Register8 PC (
    .in0(out_25), .in1(out_24), .in2(out_23), .in3(out_22), .in4(out_21), .in5(out_20), .in6(out_19),
    .in7(out_18), .read(control_1_pc_r), .write(control_1_pc_w), .reset(RESET_2_out), .out0(out_25),
    .out1(out_24), .out2(out_23), .out3(out_22), .out4(out_21), .out5(out_20), .out6(out_19), .out7(out_18));
  and and_9 (and_9_out, not_3_out, STR_out);
  Button STR (.out(STR_out));
  and and_10 (and_10_out, decoder_1_out2, control_1_rx_w);
  assign out_21 = and_7_out ? in_4 : 1'bz;  // Controlled_Buffer controlled_buffer_3
  assign out_20 = and_7_out ? in_3 : 1'bz;  // Controlled_Buffer controlled_buffer_4
  assign out_19 = and_7_out ? in_2 : 1'bz;  // Controlled_Buffer controlled_buffer_5
  assign out_18 = and_7_out ? in_1 : 1'bz;  // Controlled_Buffer controlled_buffer_6
  assign out_20 = and_9_out ? in_12 : 1'bz;  // Controlled_Buffer controlled_buffer_7
  assign out_19 = and_9_out ? in_11 : 1'bz;  // Controlled_Buffer controlled_buffer_8
  assign out_18 = and_9_out ? in_10 : 1'bz;  // Controlled_Buffer controlled_buffer_9
  assign out_21 = and_9_out ? in_13 : 1'bz;  // Controlled_Buffer controlled_buffer_10
  assign out_24 = and_7_out ? in_7 : 1'bz;  // Controlled_Buffer controlled_buffer_11
  assign out_22 = and_7_out ? in_5 : 1'bz;  // Controlled_Buffer controlled_buffer_12
  assign out_23 = and_7_out ? in_6 : 1'bz;  // Controlled_Buffer controlled_buffer_13
  assign out_25 = and_7_out ? in_8 : 1'bz;  // Controlled_Buffer controlled_buffer_14
  assign out_23 = and_9_out ? in_15 : 1'bz;  // Controlled_Buffer controlled_buffer_15
  assign out_24 = and_9_out ? in_16 : 1'bz;  // Controlled_Buffer controlled_buffer_16
  assign out_25 = and_9_out ? in_17 : 1'bz;  // Controlled_Buffer controlled_buffer_17
  assign out_22 = and_9_out ? in_14 : 1'bz;  // Controlled_Buffer controlled_buffer_18
  Register8 R3 (
    .in0(out_25), .in1(out_24), .in2(out_23), .in3(out_22), .in4(out_21), .in5(out_20), .in6(out_19),
    .in7(out_18), .read(and_12_out), .write(and_11_out), .reset(RESET_2_out), .out0(out_25), .out1(out_24),
    .out2(out_23), .out3(out_22), .out4(out_21), .out5(out_20), .out6(out_19), .out7(out_18));
  and and_11 (and_11_out, decoder_1_out3, control_1_rx_w);
  and and_12 (and_12_out, control_1_rx_r, decoder_1_out3);
  or or_4 (or_4_out, control_1_mar_w, and_7_out);
  or or_5 (or_5_out, control_1_ram_r, and_6_out);
  or or_6 (or_6_out, control_1_ram_w, and_9_out);
  or or_7 (or_7_out, and_1_out, and_7_out, and_6_out, and_9_out);
  Button RESET_3 (.out(RESET_3_out));
  Ram256 ram256_1 (
    .addr0(out_25), .addr1(out_24), .addr2(out_23), .addr3(out_22), .addr4(out_21), .addr5(out_20),
    .addr6(out_19), .addr7(out_18), .marw(or_4_out), .read(or_5_out), .write(or_6_out), .reset(RESET_3_out),
    .in0(out_25), .in1(out_24), .in2(out_23), .in3(out_22), .in4(out_21), .in5(out_20), .in6(out_19),
    .in7(out_18), .out0(out_25), .out1(out_24), .out2(out_23), .out3(out_22), .out4(out_21), .out5(out_20),
    .out6(out_19), .out7(out_18), .clk(or_7_out));

  // Notes on the sheet:
  //   0000 ra rb  ->  mov  ra, rb    ->  ra = rb
  //   0001 ra xx  ->  data ra, imm8  ->  ra = ram[pc++]
  //   0010 ra rb  ->  ldr  ra, [rb]  ->  ra = ram[rb]
  //   0011 ra rb  ->  str  ra, [rb]  ->  ram[rb] = ra
  //   0101 00 00  ->  br   imm8      ->  if true: pc = ram[pc+1]
  //   0101 00 01  ->  bz   imm8      ->  if z==1: pc = ram[pc+1]
  //   0101 00 10  ->  bnz  imm8      ->  if z==0: pc = ram[pc+1]
  //   0110 xx xx  ->  halt           ->  stop computer
  //   1000 ra rb  ->  add  ra, rb    ->  ra = ra + rb
  //   1001 ra rb  ->  sub  ra, rb    ->  ra = ra - rb
  //   1111 ra rb  ->  cmp  ra, rb    ->       ra - rb
endmodule

module Computer (
  input  in_1,
  input  in_2,
  input  in_3,
  input  in_4,
  input  in_5,
  input  in_6,
  input  in_7,
  input  in_8,
  input  in_9,
  input  in_10,
  input  in_11,
  input  in_12,
  input  in_13,
  input  in_14,
  input  in_15,
  input  in_16,
  input  in_17,
  input  in_18,
  input  in_19,
  input  in_20,
  input  in_21,
  input  in_22,
  input  in_23
);

  wire A_led0, A_led1, A_led2, A_led3, A_led4, A_led5, A_led6, A_led7, A_ledr, A_ledrst, A_ledw, A_out_0,
       A_out_1, A_out_2, A_out_3, A_out_4, A_out_5, A_out_6, A_out_7, alu_1_ledcin, alu_1_ledop, alu_1_ledz,
       alu_1_sum_0, alu_1_sum_1, alu_1_sum_2, alu_1_sum_3, alu_1_sum_4, alu_1_sum_5, alu_1_sum_6,
       alu_1_sum_7, alu_1_zero, B_led0, B_led1, B_led2, B_led3, B_led4, B_led5, B_led6, B_led7, B_leden,
       B_out_0, B_out_1, B_out_2, B_out_3, B_out_4, B_out_5, B_out_6, B_out_7, clk, controlunit_1_ledclk,
       controlunit_1_ledrst, D_led0, D_led1, D_led2, D_led3, D_led4, D_led5, D_led6, D_led7, D_ledr,
       D_ledrst, D_ledw, IR_led0, IR_led1, IR_led2, IR_led3, IR_led4, IR_led5, IR_led6, IR_led7, IR_ledr,
       IR_ledrst, IR_ledw, IR_out_0, IR_out_1, IR_out_2, IR_out_3, IR_out_4, IR_out_5, IR_out_6, IR_out_7,
       MAR_led0, MAR_led1, MAR_led2, MAR_led3, MAR_led4, MAR_led5, MAR_led6, MAR_led7, MAR_ledr, MAR_ledrst,
       MAR_ledw, MAR_out_0, MAR_out_1, MAR_out_2, MAR_out_3, MAR_out_4, MAR_out_5, MAR_out_6, MAR_out_7,
       micro, PC_led0, PC_led1, PC_led2, PC_led3, PC_led4, PC_led5, PC_led6, PC_led7, PC_ledr, PC_ledrst,
       PC_ledw, R0_led0, R0_led1, R0_led2, R0_led3, R0_led4, R0_led5, R0_led6, R0_led7, R0_ledr, R0_ledrst,
       R0_ledw, R0_out_0, R0_out_1, R0_out_2, R0_out_3, R0_out_4, R0_out_5, R0_out_6, R0_out_7, R1_led0,
       R1_led1, R1_led2, R1_led3, R1_led4, R1_led5, R1_led6, R1_led7, R1_ledr, R1_ledrst, R1_ledw, R2_led0,
       R2_led1, R2_led2, R2_led3, R2_led4, R2_led5, R2_led6, R2_led7, R2_ledr, R2_ledrst, R2_ledw, R3_led0,
       R3_led1, R3_led2, R3_led3, R3_led4, R3_led5, R3_led6, R3_led7, R3_ledr, R3_ledrst, R3_ledw, Z_led,
       Z_ledr, Z_ledrst, Z_ledw, Z_out;
  wire [7:0] memory_1_out_28, undriven;

  LED led_1 (.in(R0_ledw));
  LED led_2 (.in(R0_ledrst));
  LED led_3 (.in(R0_led7));
  LED led_4 (.in(R0_ledr));
  LED led_5 (.in(A_ledw));
  LED led_6 (.in(A_ledrst));
  LED led_7 (.in(A_led7));
  LED led_8 (.in(A_ledr));
  Reg8 R0 (
    .read(in_1), .write(in_5), .nrst(in_4), .LED7(R0_led7), .LED6(R0_led6), .LED5(R0_led5), .LED4(R0_led4),
    .LED3(R0_led3), .LED2(R0_led2), .LED1(R0_led1), .LED0(R0_led0), .IN_7(R0_out_7), .IN_6(R0_out_6),
    .IN_5(R0_out_5), .IN_4(R0_out_4), .IN_3(R0_out_3), .IN_2(R0_out_2), .IN_1(R0_out_1), .IN_0(R0_out_0),
    .OUT_7(R0_out_7), .OUT_6(R0_out_6), .OUT_5(R0_out_5), .OUT_4(R0_out_4), .OUT_3(R0_out_3),
    .OUT_2(R0_out_2), .OUT_1(R0_out_1), .OUT_0(R0_out_0), .LEDr(R0_ledr), .LEDw(R0_ledw), .LEDrst(R0_ledrst));
  LED led_9 (.in(R0_led6));
  LED led_10 (.in(R0_led3));
  LED led_11 (.in(R0_led4));
  LED led_12 (.in(R0_led5));
  Reg8 A (
    .read(1'b1), .write(in_2), .nrst(in_4), .LED7(A_led7), .LED6(A_led6), .LED5(A_led5), .LED4(A_led4),
    .LED3(A_led3), .LED2(A_led2), .LED1(A_led1), .LED0(A_led0), .IN_7(R0_out_7), .IN_6(R0_out_6),
    .IN_5(R0_out_5), .IN_4(R0_out_4), .IN_3(R0_out_3), .IN_2(R0_out_2), .IN_1(R0_out_1), .IN_0(R0_out_0),
    .OUT_7(A_out_7), .OUT_6(A_out_6), .OUT_5(A_out_5), .OUT_4(A_out_4), .OUT_3(A_out_3), .OUT_2(A_out_2),
    .OUT_1(A_out_1), .OUT_0(A_out_0), .LEDr(A_ledr), .LEDw(A_ledw), .LEDrst(A_ledrst));
  LED led_13 (.in(A_led5));
  LED led_14 (.in(A_led3));
  LED led_15 (.in(A_led6));
  LED led_16 (.in(A_led4));
  LED led_17 (.in(R0_led0));
  LED led_18 (.in(R0_led2));
  LED led_19 (.in(R0_led1));
  LED led_20 (.in(A_led1));
  LED led_21 (.in(A_led0));
  LED led_22 (.in(A_led2));
  LED led_23 (.in(D_ledw));
  LED led_24 (.in(D_ledrst));
  LED led_25 (.in(D_led7));
  LED led_26 (.in(D_ledr));
  ALU_2 alu_1 (
    .a_0(A_out_0), .a_1(A_out_1), .a_2(A_out_2), .a_3(A_out_3), .a_4(A_out_4), .a_5(A_out_5), .a_6(A_out_6),
    .a_7(A_out_7), .zero(alu_1_zero), .b_0(B_out_0), .b_1(B_out_1), .b_2(B_out_2), .b_3(B_out_3),
    .b_4(B_out_4), .b_5(B_out_5), .b_6(B_out_6), .b_7(B_out_7), .op(in_13), .cin(in_10), .sum_0(alu_1_sum_0),
    .sum_1(alu_1_sum_1), .sum_2(alu_1_sum_2), .sum_3(alu_1_sum_3), .sum_4(alu_1_sum_4), .sum_5(alu_1_sum_5),
    .sum_6(alu_1_sum_6), .sum_7(alu_1_sum_7), .LEDcin(alu_1_ledcin), .LEDop(alu_1_ledop), .LEDz(alu_1_ledz));
  LED led_27 (.in(alu_1_ledop));
  Reg8 D (
    .read(in_15), .write(in_18), .nrst(in_4), .LED7(D_led7), .LED6(D_led6), .LED5(D_led5), .LED4(D_led4),
    .LED3(D_led3), .LED2(D_led2), .LED1(D_led1), .LED0(D_led0), .IN_7(alu_1_sum_7), .IN_6(alu_1_sum_6),
    .IN_5(alu_1_sum_5), .IN_4(alu_1_sum_4), .IN_3(alu_1_sum_3), .IN_2(alu_1_sum_2), .IN_1(alu_1_sum_1),
    .IN_0(alu_1_sum_0), .OUT_7(R0_out_7), .OUT_6(R0_out_6), .OUT_5(R0_out_5), .OUT_4(R0_out_4),
    .OUT_3(R0_out_3), .OUT_2(R0_out_2), .OUT_1(R0_out_1), .OUT_0(R0_out_0), .LEDr(D_ledr), .LEDw(D_ledw),
    .LEDrst(D_ledrst));
  LED led_28 (.in(D_led6));
  LED led_29 (.in(D_led5));
  LED led_30 (.in(D_led4));
  LED led_31 (.in(R1_ledw));
  LED led_32 (.in(R1_ledrst));
  LED led_33 (.in(R1_ledr));
  LED led_34 (.in(B_leden));
  LED led_35 (.in(alu_1_ledcin));
  LED led_36 (.in(D_led0));
  LED led_37 (.in(D_led3));
  LED led_38 (.in(D_led1));
  LED led_39 (.in(D_led2));
  Reg8 R1 (
    .read(in_9), .write(in_12), .nrst(in_4), .LED7(R1_led7), .LED6(R1_led6), .LED5(R1_led5), .LED4(R1_led4),
    .LED3(R1_led3), .LED2(R1_led2), .LED1(R1_led1), .LED0(R1_led0), .IN_7(R0_out_7), .IN_6(R0_out_6),
    .IN_5(R0_out_5), .IN_4(R0_out_4), .IN_3(R0_out_3), .IN_2(R0_out_2), .IN_1(R0_out_1), .IN_0(R0_out_0),
    .OUT_7(R0_out_7), .OUT_6(R0_out_6), .OUT_5(R0_out_5), .OUT_4(R0_out_4), .OUT_3(R0_out_3),
    .OUT_2(R0_out_2), .OUT_1(R0_out_1), .OUT_0(R0_out_0), .LEDr(R1_ledr), .LEDw(R1_ledw), .LEDrst(R1_ledrst));
  LED led_40 (.in(R1_led5));
  LED led_41 (.in(R1_led6));
  LED led_42 (.in(R1_led4));
  LED led_43 (.in(R1_led7));
  ZeroPass8 B (
    .enable(in_6), .LEDen(B_leden), .LED7(B_led7), .LED6(B_led6), .LED5(B_led5), .LED4(B_led4),
    .LED3(B_led3), .LED2(B_led2), .LED1(B_led1), .LED0(B_led0), .IN_7(R0_out_7), .IN_6(R0_out_6),
    .IN_5(R0_out_5), .IN_4(R0_out_4), .IN_3(R0_out_3), .IN_2(R0_out_2), .IN_1(R0_out_1), .IN_0(R0_out_0),
    .OUT_7(B_out_7), .OUT_6(B_out_6), .OUT_5(B_out_5), .OUT_4(B_out_4), .OUT_3(B_out_3), .OUT_2(B_out_2),
    .OUT_1(B_out_1), .OUT_0(B_out_0));
  LED led_44 (.in(B_led7));
  LED led_45 (.in(B_led4));
  LED led_46 (.in(B_led5));
  LED led_47 (.in(B_led6));
  LED led_48 (.in(alu_1_ledz));
  LED led_49 (.in(R1_led3));
  LED led_50 (.in(R1_led0));
  LED led_51 (.in(R1_led2));
  LED led_52 (.in(R1_led1));
  LED led_53 (.in(B_led0));
  LED led_54 (.in(B_led3));
  LED led_55 (.in(B_led1));
  LED led_56 (.in(B_led2));
  LED led_57 (.in(Z_ledw));
  LED led_58 (.in(Z_ledrst));
  Reg1 Z (
    .IN(alu_1_zero), .read(1'b1), .write(in_20), .nrst(in_4), .LED(Z_led), .OUT(Z_out), .LEDr(Z_ledr),
    .LEDw(Z_ledw), .LEDrst(Z_ledrst));
  LED led_59 (.in(Z_led));
  LED led_60 (.in(Z_ledr));
  LED led_61 (.in(R2_ledw));
  LED led_62 (.in(R2_ledrst));
  LED led_63 (.in(R2_ledr));
  LED led_64 (.in(IR_ledw));
  LED led_65 (.in(IR_ledrst));
  LED led_66 (.in(IR_ledr));
  ControlUnit controlunit_1 (
    .INSTR_0(IR_out_0), .INSTR_1(IR_out_1), .INSTR_2(IR_out_2), .INSTR_3(IR_out_3), .INSTR_4(IR_out_4),
    .INSTR_5(IR_out_5), .INSTR_6(IR_out_6), .INSTR_7(IR_out_7), .FLAG_z(Z_out), .mINSTR(micro), .clk(clk),
    .nrst(in_4), .LEDclk(controlunit_1_ledclk), .LEDrst(controlunit_1_ledrst));
  LED led_67 (.in(controlunit_1_ledclk));
  LED led_68 (.in(controlunit_1_ledrst));
  Clock_part clock_1 (.out(clk));
  LED led_69 (.in(R2_led6));
  LED led_70 (.in(R2_led7));
  LED led_71 (.in(R2_led5));
  LED led_72 (.in(IR_led6));
  LED led_73 (.in(IR_led5));
  LED led_74 (.in(IR_led7));
  Reg8 R2 (
    .read(in_14), .write(in_17), .nrst(in_4), .LED7(R2_led7), .LED6(R2_led6), .LED5(R2_led5), .LED4(R2_led4),
    .LED3(R2_led3), .LED2(R2_led2), .LED1(R2_led1), .LED0(R2_led0), .IN_7(R0_out_7), .IN_6(R0_out_6),
    .IN_5(R0_out_5), .IN_4(R0_out_4), .IN_3(R0_out_3), .IN_2(R0_out_2), .IN_1(R0_out_1), .IN_0(R0_out_0),
    .OUT_7(R0_out_7), .OUT_6(R0_out_6), .OUT_5(R0_out_5), .OUT_4(R0_out_4), .OUT_3(R0_out_3),
    .OUT_2(R0_out_2), .OUT_1(R0_out_1), .OUT_0(R0_out_0), .LEDr(R2_ledr), .LEDw(R2_ledw), .LEDrst(R2_ledrst));
  LED led_75 (.in(R2_led3));
  LED led_76 (.in(R2_led1));
  LED led_77 (.in(R2_led2));
  LED led_78 (.in(R2_led4));
  Reg8 IR (
    .read(1'b1), .write(in_11), .nrst(in_4), .LED7(IR_led7), .LED6(IR_led6), .LED5(IR_led5), .LED4(IR_led4),
    .LED3(IR_led3), .LED2(IR_led2), .LED1(IR_led1), .LED0(IR_led0), .IN_7(R0_out_7), .IN_6(R0_out_6),
    .IN_5(R0_out_5), .IN_4(R0_out_4), .IN_3(R0_out_3), .IN_2(R0_out_2), .IN_1(R0_out_1), .IN_0(R0_out_0),
    .OUT_7(IR_out_7), .OUT_6(IR_out_6), .OUT_5(IR_out_5), .OUT_4(IR_out_4), .OUT_3(IR_out_3),
    .OUT_2(IR_out_2), .OUT_1(IR_out_1), .OUT_0(IR_out_0), .LEDr(IR_ledr), .LEDw(IR_ledw), .LEDrst(IR_ledrst));
  LED led_79 (.in(IR_led1));
  LED led_80 (.in(IR_led4));
  LED led_81 (.in(IR_led3));
  LED led_82 (.in(IR_led2));
  LED led_83 (.in(R2_led0));
  LED led_84 (.in(IR_led0));
  LED led_85 (.in(R3_ledw));
  LED led_86 (.in(R3_ledrst));
  LED led_87 (.in(R3_ledr));
  LED led_88 (.in(PC_ledw));
  LED led_89 (.in(PC_ledrst));
  LED led_90 (.in(PC_ledr));
  LED led_91 (.in(R3_led7));
  LED led_92 (.in(R3_led6));
  LED led_93 (.in(PC_led6));
  LED led_94 (.in(PC_led7));
  Reg8 R3 (
    .read(in_22), .write(in_23), .nrst(in_4), .LED7(R3_led7), .LED6(R3_led6), .LED5(R3_led5), .LED4(R3_led4),
    .LED3(R3_led3), .LED2(R3_led2), .LED1(R3_led1), .LED0(R3_led0), .IN_7(R0_out_7), .IN_6(R0_out_6),
    .IN_5(R0_out_5), .IN_4(R0_out_4), .IN_3(R0_out_3), .IN_2(R0_out_2), .IN_1(R0_out_1), .IN_0(R0_out_0),
    .OUT_7(R0_out_7), .OUT_6(R0_out_6), .OUT_5(R0_out_5), .OUT_4(R0_out_4), .OUT_3(R0_out_3),
    .OUT_2(R0_out_2), .OUT_1(R0_out_1), .OUT_0(R0_out_0), .LEDr(R3_ledr), .LEDw(R3_ledw), .LEDrst(R3_ledrst));
  LED led_95 (.in(R3_led4));
  LED led_96 (.in(R3_led3));
  LED led_97 (.in(R3_led2));
  LED led_98 (.in(R3_led5));
  Reg8 PC (
    .read(in_3), .write(in_7), .nrst(in_4), .LED7(PC_led7), .LED6(PC_led6), .LED5(PC_led5), .LED4(PC_led4),
    .LED3(PC_led3), .LED2(PC_led2), .LED1(PC_led1), .LED0(PC_led0), .IN_7(R0_out_7), .IN_6(R0_out_6),
    .IN_5(R0_out_5), .IN_4(R0_out_4), .IN_3(R0_out_3), .IN_2(R0_out_2), .IN_1(R0_out_1), .IN_0(R0_out_0),
    .OUT_7(R0_out_7), .OUT_6(R0_out_6), .OUT_5(R0_out_5), .OUT_4(R0_out_4), .OUT_3(R0_out_3),
    .OUT_2(R0_out_2), .OUT_1(R0_out_1), .OUT_0(R0_out_0), .LEDr(PC_ledr), .LEDw(PC_ledw), .LEDrst(PC_ledrst));
  LED led_99 (.in(PC_led4));
  LED led_100 (.in(PC_led3));
  LED led_101 (.in(PC_led5));
  LED led_102 (.in(PC_led2));
  LED led_103 (.in(R3_led0));
  LED led_104 (.in(R3_led1));
  LED led_105 (.in(PC_led1));
  LED led_106 (.in(PC_led0));
  LED led_107 (.in(MAR_ledw));
  LED led_108 (.in(MAR_ledrst));
  LED led_109 (.in(MAR_ledr));
  Memory_2 memory_1 (
    .ADDR_0(MAR_out_0), .ADDR_1(MAR_out_1), .ADDR_2(MAR_out_2), .ADDR_3(MAR_out_3), .ADDR_4(MAR_out_4),
    .ADDR_5(MAR_out_5), .ADDR_6(MAR_out_6), .ADDR_7(MAR_out_7), .IN_0(R0_out_0), .IN_1(R0_out_1),
    .IN_2_2(R0_out_2), .IN_3(R0_out_3), .IN_4(R0_out_4), .IN_5(R0_out_5), .IN_6(R0_out_6), .IN_7(R0_out_7),
    .OUT_0(R0_out_0), .OUT_1(R0_out_1), .OUT_2(R0_out_2), .OUT_3(R0_out_3), .OUT_4(R0_out_4),
    .OUT_5(R0_out_5), .OUT_6(R0_out_6), .OUT_7(R0_out_7), .in_2(memory_1_out_28), .in_13(undriven),
    .out_28(memory_1_out_28));  // open: rst, load_store, enable
  Reg8 MAR (
    .read(1'b1), .write(in_16), .nrst(in_4), .LED7(MAR_led7), .LED6(MAR_led6), .LED5(MAR_led5),
    .LED4(MAR_led4), .LED3(MAR_led3), .LED2(MAR_led2), .LED1(MAR_led1), .LED0(MAR_led0), .IN_7(R0_out_7),
    .IN_6(R0_out_6), .IN_5(R0_out_5), .IN_4(R0_out_4), .IN_3(R0_out_3), .IN_2(R0_out_2), .IN_1(R0_out_1),
    .IN_0(R0_out_0), .OUT_7(MAR_out_7), .OUT_6(MAR_out_6), .OUT_5(MAR_out_5), .OUT_4(MAR_out_4),
    .OUT_3(MAR_out_3), .OUT_2(MAR_out_2), .OUT_1(MAR_out_1), .OUT_0(MAR_out_0), .LEDr(MAR_ledr),
    .LEDw(MAR_ledw), .LEDrst(MAR_ledrst));
  LED led_110 (.in(MAR_led6));
  LED led_111 (.in(MAR_led5));
  LED led_112 (.in(MAR_led4));
  LED led_113 (.in(MAR_led7));
  LED led_114 (.in(MAR_led2));
  LED led_115 (.in(MAR_led0));
  LED led_116 (.in(MAR_led1));
  LED led_117 (.in(MAR_led3));
  RAM ram_1 (.addr(undriven), .data(memory_1_out_28));  // open: sel, clk, ld, clr

  // Other names for the same wires on the sheet: b_en = in_6; cin = in_10; fr_w = in_20; ir_w = in_11; ld_str = in_21;
  //   mar_w = in_16; mem_en = in_19; mem_rst = in_8; nrst = in_4; op = in_13; pc_r = in_3; pc_w = in_7; r0_r = in_1;
  //   r0_w = in_5; r1_r = in_9; r1_w = in_12; r2_r = in_14; r2_w = in_17; r3_r = in_22; r3_w = in_23; ra_w = in_2;
  //   rd_r = in_15; rd_w = in_18

  // Notes on the sheet:
  //   0000 ra rb  |  mov  ra, rb    |  ra = rb
  //   0001 ra xx  |  data ra, imm8  |  ra = ram[pc++]
  //   0010 ra rb  |  ldr  ra, [rb]  |  ra = ram[rb]
  //   0011 ra rb  |  str  ra, [rb]  |  ram[rb] = ra
  //   0101 00 00  |  br   imm8      |  if true: pc = ram[pc+1]
  //   0101 00 01  |  bz   imm8      |  if z==1: pc = ram[pc+1]
  //   0101 00 10  |  bnz  imm8      |  if z==0: pc = ram[pc+1]
  //   0110 xx xx  |  halt           |  stop computer
  //   1000 ra rb  |  add  ra, rb    |  ra = ra + rb;  (z)
  //   1001 ra rb  |  sub  ra, rb    |  ra = ra - rb;  (z)
  //   1111 ra rb  |  cmp  ra, rb    |       ra - rb;  (z)
endmodule

module ControlUnit (
  input  INSTR_0,
  input  INSTR_1,
  input  INSTR_2,
  input  INSTR_3,
  input  INSTR_4,
  input  INSTR_5,
  input  INSTR_6,
  input  INSTR_7,
  input  FLAG_z,
  input  clk,
  input  nrst,
  output LEDclk,
  output LEDrst,
  output mINSTR
);


  assign LEDclk = clk;
  assign LEDrst = nrst;
endmodule

module FullAdder (
  input  a,
  input  b,
  input  cin,
  output sum,
  output cout
);

  wire and_1_out, and_2_out, xor_1_out;

  xor xor_1 (xor_1_out, a, b);
  and and_1 (and_1_out, xor_1_out, cin);
  and and_2 (and_2_out, a, b);
  xor xor_2 (sum, xor_1_out, cin);
  or or_1 (cout, and_1_out, and_2_out);
endmodule

module Add8 (
  input  a7,
  input  b7,
  input  a6,
  input  b6,
  input  a5,
  input  b5,
  input  a4,
  input  b4,
  input  a3,
  input  b3,
  input  a2,
  input  b2,
  input  a1,
  input  b1,
  input  a0,
  input  b0,
  input  cin,
  output cout,
  output sum_7,
  output sum_6,
  output sum_5,
  output sum_4,
  output sum_3,
  output sum_2,
  output sum_1,
  output sum_0
);

  wire fulladder_2_cout, fulladder_3_cout, fulladder_4_cout, fulladder_5_cout, fulladder_6_cout,
       fulladder_7_cout, fulladder_8_cout;

  FullAdder fulladder_1 (.a(a7), .b(b7), .cin(fulladder_3_cout), .sum(sum_7), .cout(cout));
  FullAdder fulladder_2 (.a(a5), .b(b5), .cin(fulladder_4_cout), .sum(sum_5), .cout(fulladder_2_cout));
  FullAdder fulladder_3 (.a(a6), .b(b6), .cin(fulladder_2_cout), .sum(sum_6), .cout(fulladder_3_cout));
  FullAdder fulladder_4 (.a(a4), .b(b4), .cin(fulladder_5_cout), .sum(sum_4), .cout(fulladder_4_cout));
  FullAdder fulladder_5 (.a(a3), .b(b3), .cin(fulladder_6_cout), .sum(sum_3), .cout(fulladder_5_cout));
  FullAdder fulladder_6 (.a(a2), .b(b2), .cin(fulladder_7_cout), .sum(sum_2), .cout(fulladder_6_cout));
  FullAdder fulladder_7 (.a(a1), .b(b1), .cin(fulladder_8_cout), .sum(sum_1), .cout(fulladder_7_cout));
  FullAdder fulladder_8 (.a(a0), .b(b0), .cin(cin), .sum(sum_0), .cout(fulladder_8_cout));
endmodule

module Inverter8 (
  input  in_7,
  input  in_6,
  input  in_5,
  input  in_4,
  input  in_3,
  input  in_2,
  input  in_1,
  input  in_0,
  input  inv,
  output out_7,
  output out_6,
  output out_5,
  output out_4,
  output out_3,
  output out_2,
  output out_1,
  output out_0
);

  xor xor_1 (out_7, inv, in_7);
  xor xor_2 (out_5, inv, in_5);
  xor xor_3 (out_6, inv, in_6);
  xor xor_4 (out_4, inv, in_4);
  xor xor_5 (out_2, inv, in_2);
  xor xor_6 (out_3, inv, in_3);
  xor xor_7 (out_0, inv, in_0);
  xor xor_8 (out_1, inv, in_1);
endmodule

module Zero8 (
  input  _7,
  input  _6,
  input  _5,
  input  _4,
  input  _3,
  input  _2,
  input  _1,
  input  _0,
  output zero
);

  wire or_1_out, or_2_out, or_3_out, or_4_out;

  nor nor_1 (zero, or_2_out, or_1_out, or_3_out, or_4_out);
  or or_1 (or_1_out, _5, _4);
  or or_2 (or_2_out, _7, _6);
  or or_3 (or_3_out, _3, _2);
  or or_4 (or_4_out, _1, _0);
endmodule

module ALU_2 (
  input  a_0,
  input  b_0,
  input  a_1,
  input  b_1,
  input  a_2,
  input  b_2,
  input  a_3,
  input  b_3,
  input  a_4,
  input  b_4,
  input  a_5,
  input  b_5,
  input  a_6,
  input  b_6,
  input  a_7,
  input  b_7,
  input  op,
  input  cin,
  output LEDop,
  output LEDcin,
  output sum_0,
  output sum_1,
  output sum_2,
  output sum_3,
  output sum_4,
  output sum_5,
  output sum_6,
  output sum_7,
  output LEDz,
  output zero
);

  wire inverter8_1_out_0, inverter8_1_out_1, inverter8_1_out_2, inverter8_1_out_3, inverter8_1_out_4,
       inverter8_1_out_5, inverter8_1_out_6, inverter8_1_out_7, xor_1_out;

  Inverter8 inverter8_1 (
    .inv(op), .in_7(b_7), .in_6(b_6), .in_5(b_5), .in_4(b_4), .in_3(b_3), .in_2(b_2), .in_1(b_1), .in_0(b_0),
    .out_7(inverter8_1_out_7), .out_6(inverter8_1_out_6), .out_5(inverter8_1_out_5),
    .out_4(inverter8_1_out_4), .out_3(inverter8_1_out_3), .out_2(inverter8_1_out_2),
    .out_1(inverter8_1_out_1), .out_0(inverter8_1_out_0));
  Add8 add8_1 (
    .cin(xor_1_out), .a7(a_7), .b7(inverter8_1_out_7), .a6(a_6), .b6(inverter8_1_out_6), .a5(a_5),
    .b5(inverter8_1_out_5), .a4(a_4), .b4(inverter8_1_out_4), .a3(a_3), .b3(inverter8_1_out_3), .a2(a_2),
    .b2(inverter8_1_out_2), .a1(a_1), .b1(inverter8_1_out_1), .a0(a_0), .b0(inverter8_1_out_0),
    .sum_7(sum_7), .sum_6(sum_6), .sum_5(sum_5), .sum_4(sum_4), .sum_3(sum_3), .sum_2(sum_2), .sum_1(sum_1),
    .sum_0(sum_0));  // open: cout
  Zero8 zero8_1 (
    .zero(LEDz), ._7(sum_7), ._6(sum_6), ._5(sum_5), ._4(sum_4), ._3(sum_3), ._2(sum_2), ._1(sum_1),
    ._0(sum_0));
  xor xor_1 (xor_1_out, op, cin);

  assign LEDcin = cin;
  assign LEDop = op;
  assign zero = LEDz;
endmodule

module SR_Latch (
  input  set,
  input  reset,
  output Q,
  output nQ
);

  wire or_1_out, or_2_out;

  or or_1 (or_1_out, set, Q);
  not not_1 (Q, or_2_out);
  not not_2 (nQ, or_1_out);
  or or_2 (or_2_out, nQ, reset);
endmodule

module D_Latch (
  input  D,
  input  write,
  input  nrst,
  output Q,
  output nQ
);

  wire and_1_out, and_2_out, not_1_out, not_2_out, or_1_out;

  not not_1 (not_1_out, D);
  not not_2 (not_2_out, nrst);
  and and_1 (and_1_out, D, write);
  and and_2 (and_2_out, write, not_1_out);
  SR_Latch sr_latch_1 (.set(and_1_out), .Q(Q), .nQ(nQ), .reset(or_1_out));
  or or_1 (or_1_out, and_2_out, not_2_out);
endmodule

module Reg1 (
  input  IN,
  input  read,
  input  write,
  input  nrst,
  output LED,
  output OUT,
  output LEDr,
  output LEDw,
  output LEDrst
);

  D_Latch d_latch_1 (.D(IN), .write(write), .nrst(nrst), .Q(LED));  // open: nQ
  assign OUT = read ? LED : 1'bz;  // Controlled_Buffer controlled_buffer_1

  assign LEDr = read;
  assign LEDrst = nrst;
  assign LEDw = write;
endmodule

module Reg8 (
  input  IN_7,
  input  IN_6,
  input  IN_5,
  input  IN_4,
  input  IN_3,
  input  IN_2,
  input  IN_1,
  input  IN_0,
  input  read,
  input  write,
  input  nrst,
  output OUT_7,
  output OUT_6,
  output OUT_5,
  output OUT_4,
  output OUT_3,
  output OUT_2,
  output OUT_1,
  output OUT_0,
  output LEDr,
  output LEDw,
  output LEDrst,
  output LED7,
  output LED6,
  output LED5,
  output LED4,
  output LED3,
  output LED2,
  output LED1,
  output LED0
);

  Reg1 reg1_1 (
    .IN(IN_7), .read(read), .write(write), .nrst(nrst), .LED(LED7), .OUT(OUT_7));  // open: LEDr, LEDw, LEDrst
  Reg1 reg1_2 (
    .IN(IN_6), .read(read), .write(write), .nrst(nrst), .LED(LED6), .OUT(OUT_6));  // open: LEDr, LEDw, LEDrst
  Reg1 reg1_3 (
    .IN(IN_5), .read(read), .write(write), .nrst(nrst), .LED(LED5), .OUT(OUT_5));  // open: LEDr, LEDw, LEDrst
  Reg1 reg1_4 (
    .IN(IN_4), .read(read), .write(write), .nrst(nrst), .LED(LED4), .OUT(OUT_4));  // open: LEDr, LEDw, LEDrst
  Reg1 reg1_5 (
    .IN(IN_3), .read(read), .write(write), .nrst(nrst), .LED(LED3), .OUT(OUT_3));  // open: LEDr, LEDw, LEDrst
  Reg1 reg1_6 (
    .IN(IN_2), .read(read), .write(write), .nrst(nrst), .LED(LED2), .OUT(OUT_2));  // open: LEDr, LEDw, LEDrst
  Reg1 reg1_7 (
    .IN(IN_1), .read(read), .write(write), .nrst(nrst), .LED(LED1), .OUT(OUT_1));  // open: LEDr, LEDw, LEDrst
  Reg1 reg1_8 (
    .IN(IN_0), .read(read), .write(write), .nrst(nrst), .LED(LED0), .OUT(OUT_0));  // open: LEDr, LEDw, LEDrst

  assign LEDr = read;
  assign LEDrst = nrst;
  assign LEDw = write;

  // Other names for the same wires on the sheet: _0 = LED0; _1 = LED1; _2 = LED2; _3 = LED3; _4 = LED4; _5 = LED5;
  //   _6 = LED6; _7 = LED7
endmodule

module Memory_2 (
  input  ADDR_0,
  input  [7:0] in_2,
  input  IN_0,
  input  ADDR_1,
  input  IN_1,
  input  ADDR_2,
  input  IN_2_2,
  input  ADDR_3,
  input  IN_3,
  input  ADDR_4,
  input  IN_4,
  input  ADDR_5,
  input  [7:0] in_13,
  input  IN_5,
  input  ADDR_6,
  input  IN_6,
  input  ADDR_7,
  input  IN_7,
  input  rst,
  input  load_store,
  input  enable,
  output OUT_0,
  output OUT_1,
  output OUT_2,
  output OUT_3,
  output OUT_4,
  output OUT_5,
  output [7:0] out_28,
  output OUT_6,
  output OUT_7
);

  wire and_1_out, and_2_out, delayer_1_out, not_1_out, undriven, undriven_2;
  wire [7:0] ram_1_data;

  Delayer delayer_1 (.in(undriven), .out(delayer_1_out));
  RAM ram_1 (.addr(in_13), .data(ram_1_data), .sel(1'b1), .clk(delayer_1_out), .ld(not_1_out));  // open: clr
  not not_1 (not_1_out, undriven_2);
  assign ram_1_data = and_1_out ? in_2 : 8'bz;  // Controlled_Buffer controlled_buffer_1
  and and_1 (and_1_out, undriven_2, undriven);
  and and_2 (and_2_out, undriven, ~undriven_2);  // AND_Gate
  assign out_28 = and_2_out ? ram_1_data : 8'bz;  // Controlled_Buffer controlled_buffer_2
endmodule

module ZeroPass8 (
  input  IN_7,
  input  IN_6,
  input  IN_5,
  input  IN_4,
  input  IN_3,
  input  IN_2,
  input  IN_1,
  input  IN_0,
  input  enable,
  output LEDen,
  output LED7,
  output LED6,
  output LED5,
  output LED4,
  output LED3,
  output LED2,
  output LED1,
  output LED0,
  output OUT_7,
  output OUT_6,
  output OUT_5,
  output OUT_4,
  output OUT_3,
  output OUT_2,
  output OUT_1,
  output OUT_0
);

  and and_1 (LED7, enable, IN_7);
  and and_2 (LED6, enable, IN_6);
  and and_3 (LED5, enable, IN_5);
  and and_4 (LED4, enable, IN_4);
  and and_5 (LED3, enable, IN_3);
  and and_6 (LED2, enable, IN_2);
  and and_7 (LED1, enable, IN_1);
  and and_8 (LED0, enable, IN_0);

  assign LEDen = enable;
  assign OUT_0 = LED0;
  assign OUT_1 = LED1;
  assign OUT_2 = LED2;
  assign OUT_3 = LED3;
  assign OUT_4 = LED4;
  assign OUT_5 = LED5;
  assign OUT_6 = LED6;
  assign OUT_7 = LED7;
endmodule

module Delayer (
  input  in,
  output out
);

  wire not_1_out, not_2_out, not_3_out, not_4_out, not_5_out, not_6_out, not_7_out;

  not not_1 (not_1_out, in);
  not not_2 (not_2_out, not_1_out);
  not not_3 (not_3_out, not_5_out);
  not not_4 (not_4_out, not_3_out);
  not not_5 (not_5_out, not_2_out);
  not not_6 (not_6_out, not_4_out);
  not not_7 (not_7_out, not_6_out);
  not not_8 (out, not_7_out);
endmodule
